// Logisim project PRESENT.circ as structural Verilog: 3 circuits, main circuit main
module main (
);

  RAM ram_1 ();  // open: addr, data, sel, clk, ld, clr
endmodule

module S_block (
  input  [3:0] S_input,
  output [3:0] S_output
);

  Multiplexer #(.select(4), .width(4), .enable("false")) multiplexer_1 (
    .in0(4'b1100), .in1(4'b0101), .in2(4'b0110), .in3(4'b1011), .in4(4'b1001), .in5(4'b0000), .in6(4'b1010),
    .in7(4'b1101), .in8(4'b0011), .in9(4'b1110), .in10(4'b1111), .in11(4'b1000), .in12(4'b0100),
    .in13(4'b0111), .in14(4'b0001), .in15(4'b0010), .out(S_output), .sel(S_input));
endmodule

module P_block (
  input  in_1,
  input  in_2
);

  // XOR_Gate xor_1 has open pins: in1=in_1, in3=in_2, out=open
endmodule
